// Logisim project FINAL-CPU_multi.circ as structural Verilog: 1 circuit, main circuit main
module main (
);

  wire alu_1_zero_flag, clock_1_out, control_1_alu_en, control_1_alu_src, control_1_beq, control_1_bne,
       control_1_half, control_1_jal, control_1_jump, control_1_lh_lb, control_1_lui, control_1_mem_rd,
       control_1_mem_wr, control_1_memtoreg, control_1_reg_wr, control_1_regdest, control_1_sin,
       ex_mem_1_p20, ex_mem_1_p21, ex_mem_1_p22, ex_mem_1_p23, ex_mem_1_p24, ex_mem_1_p25, ex_mem_1_p26,
       ex_mem_1_p27, ex_mem_1_p28, ex_mem_1_p29, ex_mem_1_p32, id_ex_1_p22, id_ex_1_p23, id_ex_1_p24,
       id_ex_1_p25, id_ex_1_p26, id_ex_1_p27, id_ex_1_p28, id_ex_1_p29, id_ex_1_p30, id_ex_1_p31,
       id_ex_1_p32, id_ex_1_p33, id_ex_1_p34, id_ex_1_p35, main_2_pc_src, mem_wb_1_p8, mem_wb_1_p9,
       mem_wb_1_p10, mem_wb_1_p11;
  wire [2:0] alu_ctrl_1_op, id_ex_1_p41, multiplexer_2_out, multiplexer_3_out, multiplexer_4_out;
  wire [3:0] id_ex_1_p40;
  wire [11:0] ex_mem_1_p19, id_ex_1_p36;
  wire [15:0] adder_1_out, alu_1_output, bit_extender_1_out, data_mem_1_output, ex_mem_1_p18, ex_mem_1_p30,
       ex_mem_1_p31, ex_mem_1_p33, id_ex_1_p37, id_ex_1_p38, id_ex_1_p39, if_id_1_instruction_out,
       if_id_1_pc_1_out, inst_mem_1_instruction, main_1_shifted_imm, main_2_target_addr, main_3_inverse,
       main_4_lh_or_lb, mem_wb_1_p12, mem_wb_1_p13, multiplexer_1_out, multiplexer_5_out, multiplexer_6_out,
       multiplexer_7_out, multiplexer_8_out, multiplexer_9_out, PC_q, register_file_1_read_data1,
       register_file_1_read_data2;

  Multiplexer #(.width(16), .enable("false")) multiplexer_1 (
    .in0(adder_1_out), .in1(main_2_target_addr), .out(multiplexer_1_out), .sel(main_2_pc_src));
  Clock clock_1 (.out(clock_1_out));
  Register #(.width(16)) PC (.D(multiplexer_1_out), .Q(PC_q), .clk(clock_1_out));  // open: en, clr
  Adder #(.width(16)) adder_1 (.a(PC_q), .b(16'h1), .out(adder_1_out));  // open: cin, cout
  Inst_Mem inst_mem_1 (.Read_Address(PC_q), .Instruction(inst_mem_1_instruction), .clk(clock_1_out));
  IF_ID if_id_1 (
    .PC_1_in(adder_1_out), .PC_1_out(if_id_1_pc_1_out), .Instruction_in(inst_mem_1_instruction),
    .Instruction_out(if_id_1_instruction_out), .CLK(clock_1_out));
  Multiplexer #(.width(3), .enable("false")) multiplexer_2 (
    .in0(if_id_1_instruction_out[8:6]), .in1(if_id_1_instruction_out[5:3]), .out(multiplexer_2_out),
    .sel(control_1_regdest));
  Control control_1 (
    .reg_WR(control_1_reg_wr), .mem_RD(control_1_mem_rd), .mem_WR(control_1_mem_wr),
    .MemtoReg(control_1_memtoreg), .ALU_EN(control_1_alu_en), .ALU_src(control_1_alu_src),
    .LUI(control_1_lui), .JUMP(control_1_jump), .BEQ(control_1_beq), .BNE(control_1_bne),
    .JAL(control_1_jal), .RegDEST(control_1_regdest), .LH_LB(control_1_lh_lb), .HALF(control_1_half),
    .SIN(control_1_sin), .opcode(if_id_1_instruction_out[15:12]));
  Multiplexer #(.width(3), .enable("false")) multiplexer_3 (
    .in0(multiplexer_4_out), .in1(3'b111), .out(multiplexer_3_out), .sel(control_1_jal));
  Multiplexer #(.width(3), .enable("false")) multiplexer_4 (
    .in0(multiplexer_2_out), .in1(3'b001), .out(multiplexer_4_out), .sel(ex_mem_1_p23));
  assign bit_extender_1_out = {{10{if_id_1_instruction_out[5]}}, if_id_1_instruction_out[5:0]};  // Bit_Extender bit_extender_1
  Register_File register_file_1 (
    .WriteData(multiplexer_5_out), .reg_Wr(control_1_reg_wr), .CLK(clock_1_out),
    .Write_Register(multiplexer_3_out), .Read_Data1(register_file_1_read_data1),
    .Read_Data2(register_file_1_read_data2), .R1(if_id_1_instruction_out[11:9]),
    .R2(if_id_1_instruction_out[8:6]));
  Multiplexer #(.width(16), .enable("false")) multiplexer_5 (
    .in0(multiplexer_7_out), .in1(adder_1_out), .out(multiplexer_5_out), .sel(control_1_jal));
  // ID_EX id_ex_1: pin names not known; wires that end beside it: if_id_1_pc_1_out, if_id_1_instruction_out[11:0], control_1_mem_rd, control_1_mem_wr, control_1_memtoreg, control_1_alu_en, control_1_alu_src, control_1_lui, control_1_jump, control_1_beq, control_1_bne, control_1_lh_lb, control_1_half, control_1_sin, if_id_1_instruction_out[11:0], register_file_1_read_data1, register_file_1_read_data2, bit_extender_1_out, if_id_1_instruction_out[15:12], if_id_1_instruction_out[2:0], clock_1_out, id_ex_1_p22, id_ex_1_p23, id_ex_1_p24, id_ex_1_p25, id_ex_1_p26, id_ex_1_p27, id_ex_1_p28, id_ex_1_p29, id_ex_1_p30, id_ex_1_p31, id_ex_1_p32, id_ex_1_p33, id_ex_1_p34, id_ex_1_p35, id_ex_1_p36, id_ex_1_p37, id_ex_1_p38, id_ex_1_p39, id_ex_1_p40, id_ex_1_p41
  ALU_CTRL alu_ctrl_1 (.opcode(id_ex_1_p40), .func(id_ex_1_p41), .op(alu_ctrl_1_op));
  Multiplexer #(.width(16), .enable("false")) multiplexer_6 (
    .in0(id_ex_1_p38), .in1(id_ex_1_p39), .out(multiplexer_6_out), .sel(id_ex_1_p28));
  Multiplexer #(.width(16), .enable("false")) multiplexer_7 (
    .in0(multiplexer_9_out), .in1(ex_mem_1_p30), .out(multiplexer_7_out), .sel(ex_mem_1_p23));
  LUI_VALUE_main main_1 (.imm12(id_ex_1_p36), .shifted_imm(main_1_shifted_imm));
  ALU alu_1 (
    .input_1(id_ex_1_p37), .input_2(multiplexer_6_out), .alu_op(alu_ctrl_1_op), .\output (alu_1_output),
    .alu_en(id_ex_1_p27), .Zero_flag(alu_1_zero_flag));  // open: carry_out
  // EX_MEM ex_mem_1: pin names not known; wires that end beside it: id_ex_1_p22, id_ex_1_p23, id_ex_1_p24, id_ex_1_p25, id_ex_1_p26, id_ex_1_p29, id_ex_1_p30, id_ex_1_p31, id_ex_1_p32, id_ex_1_p33, id_ex_1_p34, id_ex_1_p35, main_1_shifted_imm, alu_1_output, alu_1_zero_flag, id_ex_1_p38, clock_1_out, ex_mem_1_p18, ex_mem_1_p19, ex_mem_1_p20, ex_mem_1_p21, ex_mem_1_p22, ex_mem_1_p23, ex_mem_1_p24, ex_mem_1_p25, ex_mem_1_p26, ex_mem_1_p27, ex_mem_1_p28, ex_mem_1_p29, ex_mem_1_p30, ex_mem_1_p31, ex_mem_1_p32, ex_mem_1_p33
  next_pc_main main_2 (
    .incremented_pc(ex_mem_1_p18), .imm_12(ex_mem_1_p19), .BEQ(ex_mem_1_p25), .BNE(ex_mem_1_p26),
    .JUMP(ex_mem_1_p24), .target_addr(main_2_target_addr), .PC_SRC(main_2_pc_src), .ZERO(ex_mem_1_p32));
  SIN_main main_3 (.store_value(ex_mem_1_p33), .SIN(mem_wb_1_p11), .inverse(main_3_inverse));
  Data_Mem data_mem_1 (
    .Address(ex_mem_1_p31), .mem_RD(ex_mem_1_p20), .mem_WR(ex_mem_1_p21), .WriteData(main_3_inverse),
    .Output(data_mem_1_output), .clk(clock_1_out));
  // MEM_WB mem_wb_1: pin names not known; wires that end beside it: ex_mem_1_p22, ex_mem_1_p27, ex_mem_1_p28, ex_mem_1_p29, ex_mem_1_p31, data_mem_1_output, clock_1_out, mem_wb_1_p8, mem_wb_1_p9, mem_wb_1_p10, mem_wb_1_p11, mem_wb_1_p12, mem_wb_1_p13
  Multiplexer #(.width(16), .enable("false")) multiplexer_8 (
    .in0(mem_wb_1_p12), .in1(mem_wb_1_p13), .out(multiplexer_8_out), .sel(mem_wb_1_p8));
  Multiplexer #(.width(16), .enable("false")) multiplexer_9 (
    .in0(multiplexer_8_out), .in1(main_4_lh_or_lb), .out(multiplexer_9_out), .sel(mem_wb_1_p10));
  lh_lb_main main_4 (.lh_lb(mem_wb_1_p9), .Load_Value(multiplexer_8_out), .lh_or_lb(main_4_lh_or_lb));

  // Notes on the sheet:
  //   pc+1
  //   next pc
  //   +1
  //   R-TYPE
  //   imm 12
  //   I-TYPE
  //   imm6
  //   Rt
  //   RD
  //   LUI
  //   FUNC
  //   jal
  //   pc+1
  //   LUI
  //   Reg(Rt)
  //   zero
  //   alu result
  //   load result
  //   load val
  //   lowr bye/half
  //   half
endmodule
